// Logisim project BigASM_EJ2.circ as structural Verilog
module BOARD_BIG_ASM (
  output out_1
);

  wire button_1_out, CLK, CLR, d_ff_1_q, not_1_out, Write, Write_ASCII;
  wire [6:0] ASCII;
  wire [7:0] counter_1_q;
  wire [23:0] Dir_INPUT, Dir_MEMORY;
  wire [31:0] INPUT, MEMORY_IN, MEMORY_OUT;

  Button button_1 (.out(button_1_out));
  Clock clock_1 (.out(CLK));
  D_Flip_Flop d_ff_1 (.clk(CLK), .D(1'b1), .Q(d_ff_1_q), .reset(button_1_out));  // open: Qn, preset, en
  D_Flip_Flop d_ff_2 (.clk(CLK), .D(d_ff_1_q), .Qn(CLR), .reset(button_1_out));  // open: Q, preset, en
  BIG_ASM big_asm_1 (
    .DATA_INPUT(INPUT), .MEMORY_IN(MEMORY_OUT), .CLK(CLK), .CLR(CLR), .DIR_INPUT(Dir_INPUT),
    .MEMORY_OUT(MEMORY_IN), .DIR_MEMORY(Dir_MEMORY), .Write_OUTPUT(Write), .ASCII(ASCII),
    .Write_ASCII(Write_ASCII), .END(out_1));  // open: in_2, Star
  MEMORY memory_1 (.DIR(Dir_MEMORY), .DATA_IN(MEMORY_IN), .WRITE(Write), .CLK(CLK), .CLR(CLR), .DATA_OUT(MEMORY_OUT));
  INPUT input_1 (.DIR(Dir_INPUT), .CLK(CLK), .DATA_OUT(INPUT));
  Counter counter_1 (.load(1'b0), .count(not_1_out), .Q(counter_1_q), .clk(CLK), .clr(CLR));  // open: D, carry
  not not_1 (not_1_out, out_1);
  // Probe on counter_1_q
  TTY #(.rows(32), .cols(60)) tty_1 (.data(ASCII), .clk(CLK), .we(Write_ASCII), .clr(CLR));

  // Other names for the same wires on the sheet: END = out_1

  // Notes on the sheet:
  //   COUNTER
  //   BOARD
endmodule

module INPUT (
  input  [23:0] DIR,
  input  CLK,
  output [31:0] DATA_OUT
);

  RAM #(.addrWidth(24), .dataWidth(32)) ram_1 (.addr(DIR), .data(DATA_OUT), .clk(CLK), .ld(1'b1));  // open: sel, clr
endmodule

module MEMORY (
  input  [23:0] DIR,
  input  [31:0] DATA_IN,
  input  WRITE,
  input  CLK,
  input  CLR,
  output [31:0] DATA_OUT
);

  wire not_1_out;

  not not_1 (not_1_out, WRITE);
  RAM #(.addrWidth(24), .dataWidth(32), .bus("separate")) ram_1 (
    .addr(DIR), .din(DATA_IN), .data(DATA_OUT), .clk(CLK), .ld(not_1_out), .clr(CLR));  // open: str, sel
endmodule

module BIG_ASM (
  input  [31:0] DATA_INPUT,
  input  in_2,
  input  [31:0] MEMORY_IN,
  input  CLK,
  input  CLR,
  input  Star,
  output [23:0] DIR_INPUT,
  output [31:0] MEMORY_OUT,
  output [23:0] DIR_MEMORY,
  output Write_OUTPUT,
  output [6:0] ASCII,
  output Write_ASCII,
  output END
);

  wire C____2, I____N, I_mod_j, J___I, Lc, Li, Lj, Ln, Sc, Si, Sj;
  wire [31:0] I, N;

  CONTROL_UNIT control_unit_1 (
    .Reloj(CLK), .ASCII(ASCII), .W_ASCII(Write_ASCII), .Limpiar(CLR), .Lj(Lj), .Sj(Sj), .Start(Star),
    .Lc(Lc), .Sc(Sc), .I__N(I____N), .Li(Li), .Si(Si), .J____I(J___I), .Ln(Ln), .C____2(C____2),
    .I_mod__J(I_mod_j), .I(I), .N(N), .End(END));
  DATA_PATH data_path_1 (
    .Reloj(CLK), .Limpiar(CLR), .Lc(Lc), .Sc(Sc), .I__N(I____N), .Lj(Lj), .Sj(Sj), .I_mod__J(I_mod_j),
    .Li(Li), .Si(Si), .J__I(J___I), .I(I), .Ln(Ln), .C____2(C____2), .n(DATA_INPUT), .N_2(N));

  // Other names for the same wires on the sheet: Limpiar = CLR; n_t[31:0] = DATA_INPUT; Reloj = CLK; Start = Star;
  //   W_ASCII = Write_ASCII
endmodule

module PRINT_UDEC (
  input  [31:0] num,
  input  start,
  input  CLK,
  input  RST,
  output [6:0] ASCII,
  output Write_ASCII,
  output \end 
);

  wire _0_c, _0_n, demultiplexer_1_out0, demultiplexer_2_out0, demultiplexer_2_out1, demultiplexer_3_out0,
       demultiplexer_3_out1, IDLE_2_q, IDLE_3_q, IDLE_4_q, IDLE_q, Lc, Lc_0, Ln, Ln_0, or_1_out;
  wire [23:0] bit_extender_1_out;
  wire [31:0] c, c___1, c___1_t, divider_1_rem, memory_1_data_out, multiplexer_1_out, multiplexer_2_out,
       multiplexer_3_out, n, n___10, n___10___48;

  Multiplexer #(.width(32), .enable("false")) multiplexer_1 (
    .in0(num), .in1(n___10), .out(multiplexer_1_out), .sel(Lc_0));
  Divider #(.width(32)) divider_1 (.a(n), .b(32'ha), .out(n___10), .rem(divider_1_rem));  // open: upper
  Adder #(.width(32)) adder_1 (.a(divider_1_rem), .b(32'h30), .out(n___10___48));  // open: cin, cout
  or or_1 (or_1_out, demultiplexer_1_out0, \end );
  Register #(.width(32)) u_n (.D(multiplexer_1_out), .en(Ln), .Q(n), .clk(CLK), .clr(RST));
  D_Flip_Flop IDLE (.clk(CLK), .D(or_1_out), .Q(IDLE_q), .preset(RST));  // open: Qn, en, reset
  Demultiplexer #(.enable("false")) demultiplexer_1 (
    .out0(demultiplexer_1_out0), .out1(Ln_0), .in(IDLE_q), .sel(start));
  or or_2 (Write_ASCII, demultiplexer_3_out0, demultiplexer_2_out1);
  Multiplexer #(.width(32), .enable("false")) multiplexer_2 (
    .in0(c___1), .in1(c___1_t), .out(multiplexer_2_out), .sel(Write_ASCII));
  Adder #(.width(32)) adder_2 (.a(c), .b(32'h1), .out(c___1));  // open: cin, cout
  Subtractor #(.width(32)) subtractor_1 (.a(c), .b(32'h1), .out(c___1_t));  // open: bin, bout
  D_Flip_Flop IDLE_2 (.clk(CLK), .D(Ln_0), .Q(IDLE_2_q), .reset(RST));  // open: Qn, preset, en
  Register #(.width(32)) u_c (.D(multiplexer_2_out), .en(Lc), .Q(c), .clk(CLK), .clr(RST));
  or or_3 (Lc_0, IDLE_2_q, demultiplexer_3_out1);
  Multiplexer #(.width(32), .enable("false")) multiplexer_3 (
    .in0(c), .in1(c___1_t), .out(multiplexer_3_out), .sel(Write_ASCII));
  Comparator #(.width(32), .mode("unsigned")) comparator_1 (.a({32{1'b0}}), .b(n), .lt(_0_n));  // open: gt, eq
  Comparator #(.width(32), .mode("unsigned")) comparator_2 (.a({32{1'b0}}), .b(c), .lt(_0_c));  // open: gt, eq
  D_Flip_Flop IDLE_3 (.clk(CLK), .D(Write_ASCII), .Q(IDLE_3_q), .reset(RST));  // open: Qn, preset, en
  Demultiplexer #(.enable("false")) demultiplexer_2 (
    .out0(demultiplexer_2_out0), .out1(demultiplexer_2_out1), .in(IDLE_3_q), .sel(_0_c));
  Bit_Extender #(.in_width(32), .out_width(24)) bit_extender_1 (.in(multiplexer_3_out), .out(bit_extender_1_out));
  D_Flip_Flop IDLE_4 (.clk(CLK), .D(Lc_0), .Q(IDLE_4_q), .reset(RST));  // open: Qn, preset, en
  or or_4 (Lc, Lc_0, Write_ASCII);
  or or_5 (Ln, Ln_0, Lc_0);
  Demultiplexer #(.enable("false")) demultiplexer_3 (
    .out0(demultiplexer_3_out0), .out1(demultiplexer_3_out1), .in(IDLE_4_q), .sel(_0_n));
  D_Flip_Flop IDLE_5 (.clk(CLK), .D(demultiplexer_2_out0), .Q(\end ), .reset(RST));  // open: Qn, preset, en
  MEMORY memory_1 (
    .DIR(bit_extender_1_out), .DATA_IN(n___10___48), .WRITE(Lc_0), .CLK(CLK), .CLR(RST),
    .DATA_OUT(memory_1_data_out));
  Bit_Extender #(.in_width(32), .out_width(7)) bit_extender_2 (.in(memory_1_data_out), .out(ASCII));

  // Other names for the same wires on the sheet: Lc_1 = Write_ASCII; Sc = Write_ASCII; Ln_1 = Lc_0; Sn = Lc_0;
  //   Write = Lc_0
endmodule

module PRINT_DEC (
  input  [31:0] num,
  input  start,
  input  CLK,
  input  RST,
  output [6:0] ASCII,
  output Write_ASCII,
  output END
);

  wire demultiplexer_1_out0, demultiplexer_1_out1, demultiplexer_2_out0, demultiplexer_3_out0, end_t,
       IDLE_3_q, IDLE_q, or_1_out, or_2_out, or_3_out, S_ASCII, startUDEC, Write_ASCII_1;
  wire [6:0] ASCII_t;
  wire [31:0] multiplexer_1_out, negator_1_out;

  or or_1 (or_1_out, demultiplexer_1_out0, END);
  Negator #(.width(32)) negator_1 (.in(num), .out(negator_1_out));
  D_Flip_Flop IDLE (.clk(CLK), .D(or_1_out), .Q(IDLE_q), .preset(RST));  // open: Qn, en, reset
  Demultiplexer #(.enable("false")) demultiplexer_1 (
    .out0(demultiplexer_1_out0), .out1(demultiplexer_1_out1), .in(IDLE_q), .sel(start));
  Multiplexer #(.width(32), .enable("false")) multiplexer_1 (
    .in0(num), .in1(negator_1_out), .out(multiplexer_1_out), .sel(num[31]));
  Demultiplexer #(.enable("false")) demultiplexer_2 (
    .out0(demultiplexer_2_out0), .out1(S_ASCII), .in(demultiplexer_1_out1), .sel(num[31]));
  or or_2 (or_2_out, demultiplexer_2_out0, S_ASCII);
  D_Flip_Flop IDLE_2 (.clk(CLK), .D(or_2_out), .Q(startUDEC), .reset(RST));  // open: Qn, preset, en
  PRINT_UDEC print_udec_1 (
    .num(multiplexer_1_out), .start(startUDEC), .CLK(CLK), .RST(RST), .ASCII(ASCII_t),
    .Write_ASCII(Write_ASCII_1), .\end (end_t));
  D_Flip_Flop IDLE_3 (.clk(CLK), .D(or_3_out), .Q(IDLE_3_q), .reset(RST));  // open: Qn, preset, en
  or or_3 (or_3_out, startUDEC, demultiplexer_3_out0);
  Demultiplexer #(.enable("false")) demultiplexer_3 (
    .out0(demultiplexer_3_out0), .out1(END), .in(IDLE_3_q), .sel(end_t));
  Multiplexer #(.width(7), .enable("false")) multiplexer_2 (
    .in0(ASCII_t), .in1(7'b0101101), .out(ASCII), .sel(S_ASCII));
  or or_4 (Write_ASCII, S_ASCII, Write_ASCII_1);

  // Other names for the same wires on the sheet: sign = num[31]; Write_ASCII_0 = S_ASCII
endmodule

module TEST_PRINT (
  input  [31:0] in_1,
  output out_2
);

  wire button_1_out, button_2_out, CLK, CLR, d_ff_1_q, Write_ASCII;
  wire [6:0] ASCII;

  Button button_1 (.out(button_1_out));
  Clock clock_1 (.out(CLK));
  D_Flip_Flop d_ff_1 (.clk(CLK), .D(1'b1), .Q(d_ff_1_q), .reset(button_1_out));  // open: Qn, preset, en
  D_Flip_Flop d_ff_2 (.clk(CLK), .D(d_ff_1_q), .Qn(CLR), .reset(button_1_out));  // open: Q, preset, en
  Button button_2 (.out(button_2_out));
  PRINT_UDEC print_udec_1 ();  // open: num, start, CLK, RST, ASCII, Write_ASCII, end
  PRINT_DEC print_dec_1 (
    .num(in_1), .start(button_2_out), .CLK(CLK), .RST(CLR), .ASCII(ASCII), .Write_ASCII(Write_ASCII),
    .END(out_2));
  TTY #(.rows(32), .cols(60)) tty_1 (.data(ASCII), .clk(CLK), .we(Write_ASCII), .clr(CLR));
endmodule

module DATA_PATH (
  input  Reloj,
  input  Limpiar,
  input  Lc,
  input  Sc,
  input  Lj,
  input  Sj,
  input  Li,
  input  Si,
  input  Ln,
  input  [31:0] n,
  output I__N,
  output I_mod__J,
  output J__I,
  output [31:0] I,
  output C____2,
  output [31:0] N_2
);

  wire comparator_1_eq, comparator_1_lt, comparator_2_eq, comparator_2_lt;
  wire [31:0] C, c_1, c___0, C___1, divider_1_rem, i_1, I___1, i____2, J, j_1, J___1, j___1_t,
       multiplexer_1_out, multiplexer_2_out, multiplexer_3_out;

  Comparator #(.width(32), .mode("unsigned")) comparator_1 (
    .a(I), .b(N_2), .eq(comparator_1_eq), .lt(comparator_1_lt));  // open: gt
  Comparator #(.width(32), .mode("unsigned")) comparator_2 (
    .a(J), .b(I), .eq(comparator_2_eq), .lt(comparator_2_lt));  // open: gt
  Adder #(.width(32)) adder_1 (.a(J), .b(32'h1), .out(J___1));  // open: cin, cout
  Adder #(.width(32)) adder_2 (.a(I), .b(32'h1), .out(I___1));  // open: cin, cout
  Adder #(.width(32)) adder_3 (.a(C), .b(32'h1), .out(C___1));  // open: cin, cout
  or or_1 (I__N, comparator_1_eq, comparator_1_lt);
  or or_2 (J__I, comparator_2_eq, comparator_2_lt);
  Divider #(.width(32)) divider_1 (.a(I), .b(J), .rem(divider_1_rem));  // open: out, upper
  Comparator #(.width(32), .mode("unsigned")) comparator_3 (
    .a({32{1'b0}}), .b(divider_1_rem), .eq(I_mod__J));  // open: gt, lt
  Multiplexer #(.width(32), .enable("false")) multiplexer_1 (.in0(c___0), .in1(c_1), .out(multiplexer_1_out), .sel(Sc));
  Multiplexer #(.width(32), .enable("false")) multiplexer_2 (
    .in0(j___1_t), .in1(j_1), .out(multiplexer_2_out), .sel(Si));
  Multiplexer #(.width(32), .enable("false")) multiplexer_3 (
    .in0(i____2), .in1(i_1), .out(multiplexer_3_out), .sel(Sj));
  Register #(.width(32)) u_C (.D(multiplexer_1_out), .en(Lc), .Q(C), .clk(Reloj), .clr(Limpiar));
  Register #(.width(32)) u_J (.D(multiplexer_2_out), .en(Lj), .Q(J), .clk(Reloj), .clr(Limpiar));
  Register #(.width(32)) u_I (.D(multiplexer_3_out), .en(Lj), .Q(I), .clk(Reloj), .clr(Limpiar));
  Register #(.width(32)) u_N (.D(n), .en(Ln), .Q(N_2), .clk(Reloj), .clr(Limpiar));
  Comparator #(.width(32), .mode("unsigned")) comparator_4 (.a(32'h2), .b(C), .eq(C____2));  // open: gt, lt

  // Other names for the same wires on the sheet: J____I = J__I; N_t[31:0] = N_2
endmodule

module CONTROL_UNIT (
  input  Reloj,
  input  Limpiar,
  input  Start,
  input  I__N,
  input  J____I,
  input  C____2,
  input  I_mod__J,
  input  [31:0] I,
  input  [31:0] N,
  output [6:0] ASCII,
  output W_ASCII,
  output Lj,
  output Sj,
  output Lc,
  output Sc,
  output Li,
  output Si,
  output Ln,
  output End
);

  wire d_ff_1_q, d_ff_2_q, d_ff_3_q, d_ff_4_q, d_ff_7_q, demultiplexer_1_out0, demultiplexer_2_out0,
       demultiplexer_2_out1, demultiplexer_3_out0, demultiplexer_3_out1, demultiplexer_4_out0,
       demultiplexer_4_out1, demultiplexer_5_out0, demultiplexer_6_out0, demultiplexer_7_out0,
       demultiplexer_7_out1, or_1_out, or_2_out, or_3_out, or_4_out, or_5_out, or_6_out, or_7_out;

  or or_1 (or_1_out, demultiplexer_1_out0, demultiplexer_4_out1);
  D_Flip_Flop d_ff_1 (.clk(Reloj), .D(or_1_out), .Q(d_ff_1_q), .preset(Limpiar));  // open: Qn, en, reset
  Demultiplexer #(.enable("false")) demultiplexer_1 (
    .out0(demultiplexer_1_out0), .out1(Lc), .in(d_ff_1_q), .sel(Start));
  or or_2 (or_2_out, Lc, Lc);
  Demultiplexer #(.enable("false")) demultiplexer_2 (
    .out0(demultiplexer_2_out0), .out1(demultiplexer_2_out1), .in(d_ff_2_q), .sel(I__N));
  D_Flip_Flop d_ff_2 (.clk(Reloj), .D(or_2_out), .Q(d_ff_2_q), .reset(Limpiar));  // open: Qn, preset, en
  or or_3 (or_3_out, demultiplexer_2_out1, Lc);
  or or_4 (or_4_out, demultiplexer_4_out0, demultiplexer_2_out0);
  D_Flip_Flop d_ff_3 (.D(or_4_out), .Q(d_ff_3_q), .reset(Limpiar));  // open: clk, Qn, preset, en
  Demultiplexer #(.enable("false")) demultiplexer_3 (
    .out0(demultiplexer_3_out0), .out1(demultiplexer_3_out1), .in(d_ff_4_q), .sel(J____I));
  D_Flip_Flop d_ff_4 (.clk(Reloj), .D(or_3_out), .Q(d_ff_4_q), .reset(Limpiar));  // open: Qn, preset, en
  Demultiplexer #(.enable("false")) demultiplexer_4 (
    .out0(demultiplexer_4_out0), .out1(demultiplexer_4_out1), .in(d_ff_3_q), .sel(Start));
  Demultiplexer #(.enable("false")) demultiplexer_5 (
    .out0(demultiplexer_5_out0), .out1(Lc), .in(demultiplexer_3_out0), .sel(C____2));
  Demultiplexer #(.enable("false")) demultiplexer_6 (
    .out0(demultiplexer_6_out0), .out1(Lc), .in(demultiplexer_3_out1), .sel(I_mod__J));
  or or_5 (or_5_out, demultiplexer_6_out0, Lc);
  D_Flip_Flop d_ff_5 (.clk(Reloj), .D(or_5_out), .Q(Lc), .reset(Limpiar));  // open: Qn, preset, en
  or or_6 (or_6_out, demultiplexer_5_out0, demultiplexer_7_out1);
  D_Flip_Flop d_ff_6 (.clk(Reloj), .D(or_6_out), .Q(Lc), .reset(Limpiar));  // open: Qn, preset, en
  D_Flip_Flop d_ff_7 (.clk(Reloj), .D(or_7_out), .Q(d_ff_7_q));  // open: Qn, preset, en, reset
  or or_7 (or_7_out, demultiplexer_7_out0, Lc);
  Demultiplexer #(.enable("false")) demultiplexer_7 (
    .out0(demultiplexer_7_out0), .out1(demultiplexer_7_out1), .in(d_ff_7_q), .sel(End));
  PRINT_UDEC print_udec_1 (
    .num(I), .start(Lc), .CLK(Reloj), .RST(Limpiar), .ASCII(ASCII), .Write_ASCII(W_ASCII), .\end (End));

  assign Li = Lc;
  assign Lj = Lc;
  assign Ln = Lc;
  assign Sc = Lc;
  assign Si = Lc;
  assign Sj = Lc;

  // Notes on the sheet:
  //   AFTER IF
  //   AFTER IF
  //   Es primo
endmodule
